# Fritzing sketch chickenhouse (saved by Fritzing 0.9.2b)
breadboards: 1

parts:
  Bauteil1 = Arduino Uno (Rev3)
  Bauteil2 = Arduino Ethernet Shield (Rev3)

nets:
  N1: Bauteil1.D10_PWM/SS, Bauteil2.ETH_CS
  N2: Bauteil1.D11_PWM/MOSI, Bauteil2.PWM_D11
  N3: Bauteil1.D12/MISO, Bauteil2.SPI/D12
  N4: Bauteil1.D13/SCK, Bauteil2.SPI/D13
  N5: Bauteil1.RESET, Bauteil2.RESET
  3V3: Bauteil1.3V3, Bauteil2.3V3
  5V: Bauteil1.5V, Bauteil2.5V
  GND: Bauteil1.GND, Bauteil2.GND
  VIN: Bauteil1.VIN, Bauteil2.VIN
